# Fritzing sketch stepper-motor-controlled-with-temperature (saved by Fritzing 0.9.3b)
breadboards: 1

parts:
  Part1 = Arduino Uno (Rev3) - ICSP
  M1 = Humidity and Temperature Sensor DHT11
  Part2 = Bluetooth HC-05 Macho
  R1 = Resistor [tolerance=±5% resistance=220 package=THT]
  R2 = Resistor [tolerance=±5% resistance=220 package=THT]
  MOTOR1 = 28BYJ-48 Stepper Motor
  BREAKOUT1 = ULN2003A breakout board
  VCC1 = Battery block 9V

nets:
  N1: Part1.D8, R1.Pin_0, R2.Pin_1
  N2: Part1.D9_PWM, Part2.TXD
  GND: Part1.GND, M1.NC, Part2.GND, R2.Pin_0, BREAKOUT1.0V
  N3: Part1.D2, M1.Vcc
  N4: Part1.D3_PWM, BREAKOUT1.In_4
  N5: Part1.D5_PWM, BREAKOUT1.In_2
  N6: Part1.D6_PWM, BREAKOUT1.In_3
  N7: Part1.D7, BREAKOUT1.In_1
  5V: Part1.5V, M1.Data, Part2.VCC
  N8: Part2.RXD, R1.Pin_1
  N9: MOTOR1.RED, BREAKOUT1.RED_wire
  N10: MOTOR1.ORANGE, BREAKOUT1.ORANGE_wire
  N11: MOTOR1.YELLOW, BREAKOUT1.YELLOW_wire
  N12: MOTOR1.PINK, BREAKOUT1.PINK_wire
  N13: MOTOR1.BLUE, BREAKOUT1.BLUE_wire
  N14: BREAKOUT1.+5V, VCC1.+

notes:
  Mon projet pour Mobile - MOUKHAFI Anass

custom parts:
  Humidity and Temperature Sensor DHT11: Digital relative humidity & temperature sensor DHT11
  ULN2003A breakout board: ULN2003A 7-way Darlington Transistor Driver on breakoutboard
